// Logisim project example.circ as structural Verilog: 1 circuit, main circuit main
module main (
  input  X,
  input  Y,
  input  Z,
  output OUT
);

  wire and_1_out;

  // AND_Gate and_1 has open pins: out=and_1_out
  // NOT_Gate not_1: pin names not known; wires that end beside it: Z
  // OR_Gate or_1 has open pins: out=OUT
endmodule
