// Logisim project example2.circ as structural Verilog: 1 circuit, main circuit main
module main (
  input  X,
  input  Y,
  input  Z,
  output OUT
);

  // AND_Gate and_1 has open pins: out=X
  // NOT_Gate not_1: pin names not known; wires that end beside it: X
  // OR_Gate or_1 has open pins: out=X

  assign OUT = X;
  assign Y = X;
  assign Z = X;
endmodule
