// Logisim project normal_example copy.circ as structural Verilog: 1 circuit, main circuit main
module main (
  input  A,
  input  B,
  input  C,
  output Y
);

  wire and_1_out;

  and and_1 (and_1_out, A, B);
  or or_1 (Y, and_1_out, C);
endmodule
